// Logisim project M_S_B.circ as structural Verilog: 10 circuits, main circuit main
module main (
  input  [31:0] in_1,
  input  [31:0] in_2,
  input  [3:0] in_3,
  output [31:0] out_4,
  output out_5,
  output out_6,
  output out_7,
  output out_8
);

  wire alu32_2_z, and_1_out, control_1_alu_src, control_1_aluop0, control_1_aluop1, control_1_branch,
       control_1_jump;
  wire [3:0] alu_control_1_op;
  wire [4:0] multiplexer_1_out, r_1_q_2, r_1_q_3;
  wire [5:0] r_1_q_4;
  wire [15:0] r_1_q;
  wire [27:0] shift2628_1_out_2;
  wire [31:0] adder_1_out, adder_2_out, bit_extender_1_out, multiplexer_2_out, multiplexer_3_out,
       multiplexer_4_out, r32_1_register1, r32_1_register2, shift_left_1_shift_out;

  // ALU32 alu32_1: pin names not known; wires that end beside it: in_1, in_2, in_3, out_4, out_5, out_6, out_7, out_8
  R r_1 (.D(multiplexer_4_out), .Q({r_1_q_4, r_1_q_3, r_1_q_2, r_1_q}));  // open: Clock, Reset
  Multiplexer #(.width(5)) multiplexer_1 (.in0(r_1_q_2), .in1(r_1_q[15:11]), .out(multiplexer_1_out));  // open: sel
  assign bit_extender_1_out = {{16{r_1_q[15]}}, r_1_q};  // Bit_Extender bit_extender_1
  Adder #(.width(32)) adder_1 (
    .a({r_1_q_4, r_1_q_3, r_1_q_2, r_1_q}), .b(32'h4), .out(adder_1_out));  // open: cin, cout
  Control control_1 (
    .OPCode(r_1_q_4), .Jump(control_1_jump), .Branch(control_1_branch), .ALUOP0(control_1_aluop0),
    .ALUOP1(control_1_aluop1), .ALU_SRC(control_1_alu_src));  // open: REG_Destination, MemRead, MemToReg, MemWrite, RegWrite
  R32 r32_1 (
    .MUX_IN1(r_1_q_3), .MUX_IN2(r_1_q_2), .Write_Select(multiplexer_1_out), .Register1(r32_1_register1),
    .Register2(r32_1_register2));  // open: Clock, Write_Data
  Multiplexer #(.width(32)) multiplexer_2 (
    .in0(r32_1_register2), .in1(bit_extender_1_out), .out(multiplexer_2_out), .sel(control_1_alu_src));
  shift2628 shift2628_1 (.in_1({r_1_q_3, r_1_q_2, r_1_q}), .out_2(shift2628_1_out_2));
  shift_left shift_left_1 (.Shift_in(bit_extender_1_out), .Shift_out(shift_left_1_shift_out));
  ALU_CONTROL alu_control_1 (
    .OP_1(control_1_aluop1), .OP_0(control_1_aluop0), .Funct(r_1_q[5:0]), .OP(alu_control_1_op));
  Adder #(.width(32)) adder_2 (
    .a({adder_1_out[31:28], shift2628_1_out_2}), .b(shift_left_1_shift_out), .out(adder_2_out));  // open: cin, cout
  ALU32 alu32_2 (
    .Opcode(alu_control_1_op), .A(r32_1_register1), .B(multiplexer_2_out), .Z(alu32_2_z));  // open: R, C, V, N
  and and_1 (and_1_out, control_1_branch, alu32_2_z);
  Multiplexer #(.width(32)) multiplexer_3 (
    .in0({adder_1_out[31:28], shift2628_1_out_2}), .in1(adder_2_out), .out(multiplexer_3_out), .sel(and_1_out));
  Multiplexer #(.width(32)) multiplexer_4 (
    .in0({adder_1_out[31:28], shift2628_1_out_2}), .in1(multiplexer_3_out), .out(multiplexer_4_out),
    .sel(control_1_jump));
endmodule

module One_Bit_ALU (
  input  [1:0] Operation,
  input  CarryIn,
  input  Ainvert,
  input  A,
  input  B,
  input  Binvert,
  input  Less,
  output Result,
  output CarryOut
);

  wire adder_1_out, and_1_out, multiplexer_1_out, multiplexer_2_out, not_1_out, not_2_out, or_1_out;

  not not_1 (not_1_out, B);
  Multiplexer multiplexer_1 (.in0(A), .in1(not_2_out), .out(multiplexer_1_out), .sel(Ainvert));
  not not_2 (not_2_out, A);
  Multiplexer multiplexer_2 (.in0(B), .in1(not_1_out), .out(multiplexer_2_out), .sel(Binvert));
  and and_1 (and_1_out, multiplexer_1_out, multiplexer_2_out);
  or or_1 (or_1_out, multiplexer_1_out, multiplexer_2_out);
  Adder #(.width(1)) adder_1 (
    .a(multiplexer_1_out), .b(multiplexer_2_out), .out(adder_1_out), .cin(CarryIn), .cout(CarryOut));
  Multiplexer #(.select(2)) multiplexer_3 (
    .in0(and_1_out), .in1(or_1_out), .in2(adder_1_out), .in3(Less), .out(Result), .sel(Operation));
endmodule

module ALU32 (
  input  [3:0] Opcode,
  input  [31:0] A,
  input  [31:0] B,
  output Z,
  output [31:0] R,
  output C,
  output V,
  output N
);

  wire msb_1_set, one_bit_alu_1_carryout, one_bit_alu_2_carryout, one_bit_alu_3_carryout,
       one_bit_alu_4_carryout, one_bit_alu_5_carryout, one_bit_alu_6_carryout, one_bit_alu_7_carryout,
       one_bit_alu_8_carryout, one_bit_alu_9_carryout, one_bit_alu_10_carryout, one_bit_alu_11_carryout,
       one_bit_alu_12_carryout, one_bit_alu_13_carryout, one_bit_alu_14_carryout, one_bit_alu_15_carryout,
       one_bit_alu_16_carryout, one_bit_alu_17_carryout, one_bit_alu_18_carryout, one_bit_alu_19_carryout,
       one_bit_alu_20_carryout, one_bit_alu_21_carryout, one_bit_alu_22_carryout, one_bit_alu_23_carryout,
       one_bit_alu_24_carryout, one_bit_alu_25_carryout, one_bit_alu_26_carryout, one_bit_alu_27_carryout,
       one_bit_alu_28_carryout, one_bit_alu_29_carryout, one_bit_alu_30_carryout, one_bit_alu_31_carryout;

  One_Bit_ALU one_bit_alu_1 (
    .Operation(Opcode[1:0]), .CarryIn(1'b0), .Ainvert(Opcode[3]), .A(A[0]), .B(B[0]), .Binvert(Opcode[2]),
    .Less(msb_1_set), .Result(R[0]), .CarryOut(one_bit_alu_1_carryout));
  One_Bit_ALU one_bit_alu_2 (
    .Operation(Opcode[1:0]), .CarryIn(one_bit_alu_1_carryout), .Ainvert(Opcode[3]), .A(A[1]), .B(B[1]),
    .Binvert(Opcode[2]), .Less(1'b0), .Result(R[1]), .CarryOut(one_bit_alu_2_carryout));
  One_Bit_ALU one_bit_alu_3 (
    .Operation(Opcode[1:0]), .CarryIn(one_bit_alu_2_carryout), .Ainvert(Opcode[3]), .A(A[2]), .B(B[2]),
    .Binvert(Opcode[2]), .Less(1'b0), .Result(R[2]), .CarryOut(one_bit_alu_3_carryout));
  One_Bit_ALU one_bit_alu_4 (
    .Operation(Opcode[1:0]), .CarryIn(one_bit_alu_3_carryout), .Ainvert(Opcode[3]), .A(A[3]), .B(B[3]),
    .Binvert(Opcode[2]), .Less(1'b0), .Result(R[3]), .CarryOut(one_bit_alu_4_carryout));
  One_Bit_ALU one_bit_alu_5 (
    .Operation(Opcode[1:0]), .CarryIn(one_bit_alu_4_carryout), .Ainvert(Opcode[3]), .A(A[4]), .B(B[4]),
    .Binvert(Opcode[2]), .Less(1'b0), .Result(R[4]), .CarryOut(one_bit_alu_5_carryout));
  One_Bit_ALU one_bit_alu_6 (
    .Operation(Opcode[1:0]), .CarryIn(one_bit_alu_5_carryout), .Ainvert(Opcode[3]), .A(A[5]), .B(B[5]),
    .Binvert(Opcode[2]), .Less(1'b0), .Result(R[5]), .CarryOut(one_bit_alu_6_carryout));
  One_Bit_ALU one_bit_alu_7 (
    .Operation(Opcode[1:0]), .CarryIn(one_bit_alu_6_carryout), .Ainvert(Opcode[3]), .A(A[6]), .B(B[6]),
    .Binvert(Opcode[2]), .Less(1'b0), .Result(R[6]), .CarryOut(one_bit_alu_7_carryout));
  One_Bit_ALU one_bit_alu_8 (
    .Operation(Opcode[1:0]), .CarryIn(one_bit_alu_7_carryout), .Ainvert(Opcode[3]), .A(A[7]), .B(B[7]),
    .Binvert(Opcode[2]), .Less(1'b0), .Result(R[7]), .CarryOut(one_bit_alu_8_carryout));
  One_Bit_ALU one_bit_alu_9 (
    .Operation(Opcode[1:0]), .CarryIn(one_bit_alu_8_carryout), .Ainvert(Opcode[3]), .A(A[8]), .B(B[8]),
    .Binvert(Opcode[2]), .Less(1'b0), .Result(R[8]), .CarryOut(one_bit_alu_9_carryout));
  One_Bit_ALU one_bit_alu_10 (
    .Operation(Opcode[1:0]), .CarryIn(one_bit_alu_9_carryout), .Ainvert(Opcode[3]), .A(A[9]), .B(B[9]),
    .Binvert(Opcode[2]), .Less(1'b0), .Result(R[9]), .CarryOut(one_bit_alu_10_carryout));
  One_Bit_ALU one_bit_alu_11 (
    .Operation(Opcode[1:0]), .CarryIn(one_bit_alu_10_carryout), .Ainvert(Opcode[3]), .A(A[10]), .B(B[10]),
    .Binvert(Opcode[2]), .Less(1'b0), .Result(R[10]), .CarryOut(one_bit_alu_11_carryout));
  One_Bit_ALU one_bit_alu_12 (
    .Operation(Opcode[1:0]), .CarryIn(one_bit_alu_11_carryout), .Ainvert(Opcode[3]), .A(A[11]), .B(B[11]),
    .Binvert(Opcode[2]), .Less(1'b0), .Result(R[11]), .CarryOut(one_bit_alu_12_carryout));
  One_Bit_ALU one_bit_alu_13 (
    .Operation(Opcode[1:0]), .CarryIn(one_bit_alu_12_carryout), .Ainvert(Opcode[3]), .A(A[12]), .B(B[12]),
    .Binvert(Opcode[2]), .Less(1'b0), .Result(R[12]), .CarryOut(one_bit_alu_13_carryout));
  One_Bit_ALU one_bit_alu_14 (
    .Operation(Opcode[1:0]), .CarryIn(one_bit_alu_13_carryout), .Ainvert(Opcode[3]), .A(A[13]), .B(B[13]),
    .Binvert(Opcode[2]), .Less(1'b0), .Result(R[13]), .CarryOut(one_bit_alu_14_carryout));
  One_Bit_ALU one_bit_alu_15 (
    .Operation(Opcode[1:0]), .CarryIn(one_bit_alu_14_carryout), .Ainvert(Opcode[3]), .A(A[14]), .B(B[14]),
    .Binvert(Opcode[2]), .Less(1'b0), .Result(R[14]), .CarryOut(one_bit_alu_15_carryout));
  One_Bit_ALU one_bit_alu_16 (
    .Operation(Opcode[1:0]), .CarryIn(one_bit_alu_15_carryout), .Ainvert(Opcode[3]), .A(A[15]), .B(B[15]),
    .Binvert(Opcode[2]), .Less(1'b0), .Result(R[15]), .CarryOut(one_bit_alu_16_carryout));
  One_Bit_ALU one_bit_alu_17 (
    .Operation(Opcode[1:0]), .CarryIn(one_bit_alu_16_carryout), .Ainvert(Opcode[3]), .A(A[16]), .B(B[16]),
    .Binvert(Opcode[2]), .Less(1'b0), .Result(R[16]), .CarryOut(one_bit_alu_17_carryout));
  One_Bit_ALU one_bit_alu_18 (
    .Operation(Opcode[1:0]), .CarryIn(one_bit_alu_17_carryout), .Ainvert(Opcode[3]), .A(A[17]), .B(B[17]),
    .Binvert(Opcode[2]), .Less(1'b0), .Result(R[17]), .CarryOut(one_bit_alu_18_carryout));
  One_Bit_ALU one_bit_alu_19 (
    .Operation(Opcode[1:0]), .CarryIn(one_bit_alu_18_carryout), .Ainvert(Opcode[3]), .A(A[18]), .B(B[18]),
    .Binvert(Opcode[2]), .Less(1'b0), .Result(R[18]), .CarryOut(one_bit_alu_19_carryout));
  One_Bit_ALU one_bit_alu_20 (
    .Operation(Opcode[1:0]), .CarryIn(one_bit_alu_19_carryout), .Ainvert(Opcode[3]), .A(A[19]), .B(B[19]),
    .Binvert(Opcode[2]), .Less(1'b0), .Result(R[19]), .CarryOut(one_bit_alu_20_carryout));
  One_Bit_ALU one_bit_alu_21 (
    .Operation(Opcode[1:0]), .CarryIn(one_bit_alu_20_carryout), .Ainvert(Opcode[3]), .A(A[20]), .B(B[20]),
    .Binvert(Opcode[2]), .Less(1'b0), .Result(R[20]), .CarryOut(one_bit_alu_21_carryout));
  One_Bit_ALU one_bit_alu_22 (
    .Operation(Opcode[1:0]), .CarryIn(one_bit_alu_21_carryout), .Ainvert(Opcode[3]), .A(A[21]), .B(B[21]),
    .Binvert(Opcode[2]), .Less(1'b0), .Result(R[21]), .CarryOut(one_bit_alu_22_carryout));
  One_Bit_ALU one_bit_alu_23 (
    .Operation(Opcode[1:0]), .CarryIn(one_bit_alu_22_carryout), .Ainvert(Opcode[3]), .A(A[22]), .B(B[22]),
    .Binvert(Opcode[2]), .Less(1'b0), .Result(R[22]), .CarryOut(one_bit_alu_23_carryout));
  One_Bit_ALU one_bit_alu_24 (
    .Operation(Opcode[1:0]), .CarryIn(one_bit_alu_23_carryout), .Ainvert(Opcode[3]), .A(A[23]), .B(B[23]),
    .Binvert(Opcode[2]), .Less(1'b0), .Result(R[23]), .CarryOut(one_bit_alu_24_carryout));
  One_Bit_ALU one_bit_alu_25 (
    .Operation(Opcode[1:0]), .CarryIn(one_bit_alu_24_carryout), .Ainvert(Opcode[3]), .A(A[24]), .B(B[24]),
    .Binvert(Opcode[2]), .Less(1'b0), .Result(R[24]), .CarryOut(one_bit_alu_25_carryout));
  One_Bit_ALU one_bit_alu_26 (
    .Operation(Opcode[1:0]), .CarryIn(one_bit_alu_25_carryout), .Ainvert(Opcode[3]), .A(A[25]), .B(B[25]),
    .Binvert(Opcode[2]), .Less(1'b0), .Result(R[25]), .CarryOut(one_bit_alu_26_carryout));
  One_Bit_ALU one_bit_alu_27 (
    .Operation(Opcode[1:0]), .CarryIn(one_bit_alu_26_carryout), .Ainvert(Opcode[3]), .A(A[26]), .B(B[26]),
    .Binvert(Opcode[2]), .Less(1'b0), .Result(R[26]), .CarryOut(one_bit_alu_27_carryout));
  One_Bit_ALU one_bit_alu_28 (
    .Operation(Opcode[1:0]), .CarryIn(one_bit_alu_27_carryout), .Ainvert(Opcode[3]), .A(A[27]), .B(B[27]),
    .Binvert(Opcode[2]), .Less(1'b0), .Result(R[27]), .CarryOut(one_bit_alu_28_carryout));
  One_Bit_ALU one_bit_alu_29 (
    .Operation(Opcode[1:0]), .CarryIn(one_bit_alu_28_carryout), .Ainvert(Opcode[3]), .A(A[28]), .B(B[28]),
    .Binvert(Opcode[2]), .Less(1'b0), .Result(R[28]), .CarryOut(one_bit_alu_29_carryout));
  One_Bit_ALU one_bit_alu_30 (
    .Operation(Opcode[1:0]), .CarryIn(one_bit_alu_29_carryout), .Ainvert(Opcode[3]), .A(A[29]), .B(B[29]),
    .Binvert(Opcode[2]), .Less(1'b0), .Result(R[29]), .CarryOut(one_bit_alu_30_carryout));
  One_Bit_ALU one_bit_alu_31 (
    .Operation(Opcode[1:0]), .CarryIn(one_bit_alu_30_carryout), .Ainvert(Opcode[3]), .A(A[30]), .B(B[30]),
    .Binvert(Opcode[2]), .Less(1'b0), .Result(R[30]), .CarryOut(one_bit_alu_31_carryout));
  MSB msb_1 (
    .Operation(Opcode[1:0]), .CarryIn(one_bit_alu_31_carryout), .Ainvert(Opcode[3]), .A(A[31]), .B(B[31]),
    .Binvert(Opcode[2]), .Less(1'b0), .Result(N), .CarryOut(C), .Set(msb_1_set), .Overflow(V));
  nor nor_1 (Z, R[0], R[1], R[2], R[3], R[4], R[5], R[6], R[7], R[8], R[9], R[10], R[11], R[12], R[13], R[14], R[15], R[16], R[17], R[18], R[19], R[20], R[21], R[22], R[23], R[24], R[25], R[26], R[27], R[28], R[29], R[30], N);

  assign R[31] = N;

  // Other names for the same wires on the sheet: R31 = N
endmodule

module MSB (
  input  [1:0] Operation,
  input  CarryIn,
  input  Ainvert,
  input  A,
  input  B,
  input  Binvert,
  input  Less,
  output Result,
  output CarryOut,
  output Set,
  output Overflow
);

  wire and_1_out, and_2_out, and_3_out, multiplexer_1_out, multiplexer_2_out, not_1_out, not_2_out,
       not_3_out, or_1_out;

  Multiplexer multiplexer_1 (.in0(A), .in1(not_1_out), .out(multiplexer_1_out), .sel(Ainvert));
  not not_1 (not_1_out, A);
  Multiplexer multiplexer_2 (.in0(B), .in1(not_2_out), .out(multiplexer_2_out), .sel(Binvert));
  not not_2 (not_2_out, B);
  not not_3 (not_3_out, Set);
  and and_1 (and_1_out, A, B, not_3_out);
  and and_2 (and_2_out, not_1_out, not_2_out, Set);
  and and_3 (and_3_out, multiplexer_1_out, multiplexer_2_out);
  or or_1 (or_1_out, multiplexer_1_out, multiplexer_2_out);
  or or_2 (Overflow, and_1_out, and_2_out);
  Adder #(.width(1)) adder_1 (.a(multiplexer_1_out), .b(multiplexer_2_out), .out(Set), .cin(CarryIn), .cout(CarryOut));
  Multiplexer #(.select(2)) multiplexer_3 (
    .in0(and_3_out), .in1(or_1_out), .in2(Set), .in3(Less), .out(Result), .sel(Operation));
endmodule

module R (
  input  [31:0] D,
  input  Clock,
  input  Reset,
  output [31:0] Q
);

  D_Flip_Flop d_ff_1 (.D(D[0]), .clk(Clock), .Q(Q[0]), .reset(Reset));  // open: Qn, preset
  D_Flip_Flop d_ff_2 (.D(D[1]), .clk(Clock), .Q(Q[1]), .reset(Reset));  // open: Qn, preset
  D_Flip_Flop d_ff_3 (.D(D[2]), .clk(Clock), .Q(Q[2]), .reset(Reset));  // open: Qn, preset
  D_Flip_Flop d_ff_4 (.D(D[3]), .clk(Clock), .Q(Q[3]), .reset(Reset));  // open: Qn, preset
  D_Flip_Flop d_ff_5 (.D(D[4]), .clk(Clock), .Q(Q[4]), .reset(Reset));  // open: Qn, preset
  D_Flip_Flop d_ff_6 (.D(D[5]), .clk(Clock), .Q(Q[5]), .reset(Reset));  // open: Qn, preset
  D_Flip_Flop d_ff_7 (.D(D[6]), .clk(Clock), .Q(Q[6]), .reset(Reset));  // open: Qn, preset
  D_Flip_Flop d_ff_8 (.D(D[7]), .clk(Clock), .Q(Q[7]), .reset(Reset));  // open: Qn, preset
  D_Flip_Flop d_ff_9 (.D(D[8]), .clk(Clock), .Q(Q[8]), .reset(Reset));  // open: Qn, preset
  D_Flip_Flop d_ff_10 (.D(D[9]), .clk(Clock), .Q(Q[9]), .reset(Reset));  // open: Qn, preset
  D_Flip_Flop d_ff_11 (.D(D[10]), .clk(Clock), .Q(Q[10]), .reset(Reset));  // open: Qn, preset
  D_Flip_Flop d_ff_12 (.D(D[11]), .clk(Clock), .Q(Q[11]), .reset(Reset));  // open: Qn, preset
  D_Flip_Flop d_ff_13 (.D(D[12]), .clk(Clock), .Q(Q[12]), .reset(Reset));  // open: Qn, preset
  D_Flip_Flop d_ff_14 (.D(D[13]), .clk(Clock), .Q(Q[13]), .reset(Reset));  // open: Qn, preset
  D_Flip_Flop d_ff_15 (.D(D[14]), .clk(Clock), .Q(Q[14]), .reset(Reset));  // open: Qn, preset
  D_Flip_Flop d_ff_16 (.D(D[15]), .clk(Clock), .Q(Q[15]), .reset(Reset));  // open: Qn, preset
  D_Flip_Flop d_ff_17 (.D(D[16]), .clk(Clock), .Q(Q[16]), .reset(Reset));  // open: Qn, preset
  D_Flip_Flop d_ff_18 (.D(D[17]), .clk(Clock), .Q(Q[17]), .reset(Reset));  // open: Qn, preset
  D_Flip_Flop d_ff_19 (.D(D[18]), .clk(Clock), .Q(Q[18]), .reset(Reset));  // open: Qn, preset
  D_Flip_Flop d_ff_20 (.D(D[19]), .clk(Clock), .Q(Q[19]), .reset(Reset));  // open: Qn, preset
  D_Flip_Flop d_ff_21 (.D(D[20]), .clk(Clock), .Q(Q[20]), .reset(Reset));  // open: Qn, preset
  D_Flip_Flop d_ff_22 (.D(D[21]), .clk(Clock), .Q(Q[21]), .reset(Reset));  // open: Qn, preset
  D_Flip_Flop d_ff_23 (.D(D[22]), .clk(Clock), .Q(Q[22]), .reset(Reset));  // open: Qn, preset
  D_Flip_Flop d_ff_24 (.D(D[23]), .clk(Clock), .Q(Q[23]), .reset(Reset));  // open: Qn, preset
  D_Flip_Flop d_ff_25 (.D(D[24]), .clk(Clock), .Q(Q[24]), .reset(Reset));  // open: Qn, preset
  D_Flip_Flop d_ff_26 (.D(D[25]), .clk(Clock), .Q(Q[25]), .reset(Reset));  // open: Qn, preset
  D_Flip_Flop d_ff_27 (.D(D[26]), .clk(Clock), .Q(Q[26]), .reset(Reset));  // open: Qn, preset
  D_Flip_Flop d_ff_28 (.D(D[27]), .clk(Clock), .Q(Q[27]), .reset(Reset));  // open: Qn, preset
  D_Flip_Flop d_ff_29 (.D(D[28]), .clk(Clock), .Q(Q[28]), .reset(Reset));  // open: Qn, preset
  D_Flip_Flop d_ff_30 (.D(D[29]), .clk(Clock), .Q(Q[29]), .reset(Reset));  // open: Qn, preset
  D_Flip_Flop d_ff_31 (.D(D[30]), .clk(Clock), .Q(Q[30]), .reset(Reset));  // open: Qn, preset
  D_Flip_Flop d_ff_32 (.D(D[31]), .clk(Clock), .Q(Q[31]), .reset(Reset));  // open: Qn, preset
endmodule

module R32 (
  input  [4:0] MUX_IN1,
  input  [4:0] MUX_IN2,
  input  Clock,
  input  [4:0] Write_Select,
  input  [31:0] Write_Data,
  output [31:0] Register1,
  output [31:0] Register2
);

  wire and_1_out, and_2_out, and_3_out, and_4_out, and_5_out, and_6_out, and_7_out, and_8_out, and_9_out,
       and_10_out, and_11_out, and_12_out, and_13_out, and_14_out, and_15_out, and_16_out, and_17_out,
       and_18_out, and_19_out, and_20_out, and_21_out, and_22_out, and_23_out, and_24_out, and_25_out,
       and_26_out, and_27_out, and_28_out, and_29_out, and_30_out, and_31_out, and_32_out, decoder_1_out0,
       decoder_1_out1, decoder_1_out2, decoder_1_out3, decoder_1_out4, decoder_1_out5, decoder_1_out6,
       decoder_1_out8, decoder_1_out9, decoder_1_out10, decoder_1_out11, decoder_1_out12, decoder_1_out13,
       decoder_1_out14, decoder_1_out15, decoder_1_out16, decoder_1_out17, decoder_1_out18, decoder_1_out19,
       decoder_1_out20, decoder_1_out21, decoder_1_out22, decoder_1_out23, decoder_1_out24, decoder_1_out25,
       decoder_1_out26, decoder_1_out27, decoder_1_out28, decoder_1_out29, decoder_1_out30, decoder_1_out31,
       undriven;
  wire [31:0] r_1_q, r_2_q, r_3_q, r_4_q, r_5_q, r_6_q, r_7_q, r_8_q, r_9_q, r_10_q, r_11_q, r_12_q, r_13_q,
       r_14_q, r_15_q, r_16_q, r_17_q, r_18_q, r_19_q, r_20_q, r_21_q, r_22_q, r_23_q, r_24_q, r_25_q,
       r_26_q, r_27_q, r_28_q, r_29_q, r_30_q, r_31_q, r_32_q;

  Decoder #(.select(5)) decoder_1 (
    .out0(decoder_1_out0), .out1(decoder_1_out1), .out2(decoder_1_out2), .out3(decoder_1_out3),
    .out4(decoder_1_out4), .out5(decoder_1_out5), .out6(decoder_1_out6), .out7(decoder_1_out6),
    .out8(decoder_1_out8), .out9(decoder_1_out9), .out10(decoder_1_out10), .out11(decoder_1_out11),
    .out12(decoder_1_out12), .out13(decoder_1_out13), .out14(decoder_1_out14), .out15(decoder_1_out15),
    .out16(decoder_1_out16), .out17(decoder_1_out17), .out18(decoder_1_out18), .out19(decoder_1_out19),
    .out20(decoder_1_out20), .out21(decoder_1_out21), .out22(decoder_1_out22), .out23(decoder_1_out23),
    .out24(decoder_1_out24), .out25(decoder_1_out25), .out26(decoder_1_out26), .out27(decoder_1_out27),
    .out28(decoder_1_out28), .out29(decoder_1_out29), .out30(decoder_1_out30), .out31(decoder_1_out31),
    .sel(Write_Select), .en(undriven));
  and and_1 (and_1_out, Clock, decoder_1_out0);
  and and_2 (and_2_out, Clock, decoder_1_out1);
  and and_3 (and_3_out, Clock, decoder_1_out2);
  and and_4 (and_4_out, Clock, decoder_1_out3);
  and and_5 (and_5_out, Clock, decoder_1_out4);
  and and_6 (and_6_out, Clock, decoder_1_out5);
  and and_7 (and_7_out, Clock, decoder_1_out6);
  and and_8 (and_8_out, Clock, decoder_1_out6);
  and and_9 (and_9_out, Clock, decoder_1_out8);
  and and_10 (and_10_out, Clock, decoder_1_out9);
  and and_11 (and_11_out, Clock, decoder_1_out10);
  and and_12 (and_12_out, Clock, decoder_1_out11);
  and and_13 (and_13_out, Clock, decoder_1_out12);
  and and_14 (and_14_out, Clock, decoder_1_out13);
  and and_15 (and_15_out, Clock, decoder_1_out14);
  and and_16 (and_16_out, Clock, decoder_1_out15);
  and and_17 (and_17_out, Clock, decoder_1_out16);
  and and_18 (and_18_out, Clock, decoder_1_out17);
  and and_19 (and_19_out, Clock, decoder_1_out18);
  and and_20 (and_20_out, Clock, decoder_1_out19);
  and and_21 (and_21_out, Clock, decoder_1_out20);
  and and_22 (and_22_out, Clock, decoder_1_out21);
  and and_23 (and_23_out, Clock, decoder_1_out22);
  and and_24 (and_24_out, Clock, decoder_1_out23);
  and and_25 (and_25_out, Clock, decoder_1_out24);
  and and_26 (and_26_out, Clock, decoder_1_out25);
  and and_27 (and_27_out, Clock, decoder_1_out26);
  and and_28 (and_28_out, Clock, decoder_1_out27);
  and and_29 (and_29_out, Clock, decoder_1_out28);
  and and_30 (and_30_out, Clock, decoder_1_out29);
  and and_31 (and_31_out, Clock, decoder_1_out30);
  and and_32 (and_32_out, Clock, decoder_1_out31);
  R r_1 (.D(Write_Data), .Clock(and_1_out), .Q(r_1_q));  // open: Reset
  R r_2 (.D(Write_Data), .Clock(and_2_out), .Q(r_2_q));  // open: Reset
  R r_3 (.D(Write_Data), .Clock(and_3_out), .Q(r_3_q));  // open: Reset
  R r_4 (.D(Write_Data), .Clock(and_4_out), .Q(r_4_q));  // open: Reset
  R r_5 (.D(Write_Data), .Clock(and_5_out), .Q(r_5_q));  // open: Reset
  R r_6 (.D(Write_Data), .Clock(and_6_out), .Q(r_6_q));  // open: Reset
  R r_7 (.D(Write_Data), .Clock(and_7_out), .Q(r_7_q));  // open: Reset
  R r_8 (.D(Write_Data), .Clock(and_8_out), .Q(r_8_q));  // open: Reset
  R r_9 (.D(Write_Data), .Clock(and_9_out), .Q(r_9_q));  // open: Reset
  R r_10 (.D(Write_Data), .Clock(and_10_out), .Q(r_10_q));  // open: Reset
  R r_11 (.D(Write_Data), .Clock(and_11_out), .Q(r_11_q));  // open: Reset
  R r_12 (.D(Write_Data), .Clock(and_12_out), .Q(r_12_q));  // open: Reset
  R r_13 (.D(Write_Data), .Clock(and_13_out), .Q(r_13_q));  // open: Reset
  R r_14 (.D(Write_Data), .Clock(and_14_out), .Q(r_14_q));  // open: Reset
  R r_15 (.D(Write_Data), .Clock(and_15_out), .Q(r_15_q));  // open: Reset
  R r_16 (.D(Write_Data), .Clock(and_16_out), .Q(r_16_q));  // open: Reset
  R r_17 (.D(Write_Data), .Clock(and_17_out), .Q(r_17_q));  // open: Reset
  R r_18 (.D(Write_Data), .Clock(and_18_out), .Q(r_18_q));  // open: Reset
  R r_19 (.D(Write_Data), .Clock(and_19_out), .Q(r_19_q));  // open: Reset
  R r_20 (.D(Write_Data), .Clock(and_20_out), .Q(r_20_q));  // open: Reset
  R r_21 (.D(Write_Data), .Clock(and_21_out), .Q(r_21_q));  // open: Reset
  R r_22 (.D(Write_Data), .Clock(and_22_out), .Q(r_22_q));  // open: Reset
  R r_23 (.D(Write_Data), .Clock(and_23_out), .Q(r_23_q));  // open: Reset
  R r_24 (.D(Write_Data), .Clock(and_24_out), .Q(r_24_q));  // open: Reset
  R r_25 (.D(Write_Data), .Clock(and_25_out), .Q(r_25_q));  // open: Reset
  R r_26 (.D(Write_Data), .Clock(and_26_out), .Q(r_26_q));  // open: Reset
  R r_27 (.D(Write_Data), .Clock(and_27_out), .Q(r_27_q));  // open: Reset
  R r_28 (.D(Write_Data), .Clock(and_28_out), .Q(r_28_q));  // open: Reset
  R r_29 (.D(Write_Data), .Clock(and_29_out), .Q(r_29_q));  // open: Reset
  R r_30 (.D(Write_Data), .Clock(and_30_out), .Q(r_30_q));  // open: Reset
  R r_31 (.D(Write_Data), .Clock(and_31_out), .Q(r_31_q));  // open: Reset
  R r_32 (.D(Write_Data), .Clock(and_32_out), .Q(r_32_q));  // open: Reset
  Multiplexer #(.select(5), .width(32)) multiplexer_1 (
    .in0(r_1_q), .in1(r_2_q), .in2(r_3_q), .in3(r_4_q), .in4(r_5_q), .in5(r_6_q), .in6(r_7_q), .in7(r_8_q),
    .in8(r_9_q), .in9(r_10_q), .in10(r_11_q), .in11(r_12_q), .in12(r_13_q), .in13(r_14_q), .in14(r_15_q),
    .in15(r_16_q), .in16(r_17_q), .in17(r_18_q), .in18(r_19_q), .in19(r_20_q), .in20(r_21_q), .in21(r_22_q),
    .in22(r_23_q), .in23(r_24_q), .in24(r_25_q), .in25(r_26_q), .in26(r_27_q), .in27(r_28_q), .in28(r_29_q),
    .in29(r_30_q), .in30(r_31_q), .in31(r_32_q), .out(Register1), .sel(MUX_IN1));
  Multiplexer #(.select(5), .width(32)) multiplexer_2 (
    .in0(r_1_q), .in1(r_2_q), .in2(r_3_q), .in3(r_4_q), .in4(r_5_q), .in5(r_6_q), .in6(r_7_q), .in7(r_8_q),
    .in8(r_9_q), .in9(r_10_q), .in10(r_11_q), .in11(r_12_q), .in12(r_13_q), .in13(r_14_q), .in14(r_15_q),
    .in15(r_16_q), .in16(r_17_q), .in17(r_18_q), .in18(r_19_q), .in19(r_20_q), .in20(r_21_q), .in21(r_22_q),
    .in22(r_23_q), .in23(r_24_q), .in24(r_25_q), .in25(r_26_q), .in26(r_27_q), .in27(r_28_q), .in28(r_29_q),
    .in29(r_30_q), .in30(r_31_q), .in31(r_32_q), .out(Register2), .sel(MUX_IN2));
endmodule

module Control (
  input  [5:0] OPCode,
  output REG_Destination,
  output Jump,
  output Branch,
  output MemRead,
  output MemToReg,
  output ALUOP0,
  output ALUOP1,
  output MemWrite,
  output ALU_SRC,
  output RegWrite
);

  and R_format (ALUOP0, ~OPCode[5], ~OPCode[4], ~OPCode[3], ~OPCode[2], ~OPCode[1], ~OPCode[0]);  // AND_Gate
  and lw (MemRead, OPCode[5], ~OPCode[4], ~OPCode[3], ~OPCode[2], OPCode[1], OPCode[0]);  // AND_Gate
  and sw (MemWrite, OPCode[5], ~OPCode[4], OPCode[3], ~OPCode[2], OPCode[1], OPCode[0]);  // AND_Gate
  and beq (ALUOP1, ~OPCode[5], ~OPCode[4], ~OPCode[3], OPCode[2], ~OPCode[1], ~OPCode[0]);  // AND_Gate
  and J (Jump, ~OPCode[5], ~OPCode[4], ~OPCode[3], ~OPCode[2], OPCode[1], ~OPCode[0]);  // AND_Gate
  or or_1 (ALU_SRC, MemRead, MemWrite);
  or or_2 (RegWrite, ALUOP0, MemRead);

  assign Branch = ALUOP1;
  assign MemToReg = MemRead;
  assign REG_Destination = ALUOP0;
endmodule

module ALU_CONTROL (
  input  OP_1,
  input  OP_0,
  input  [5:0] Funct,
  output [3:0] OP
);

  wire and_1_out, and_2_out, and_3_out, and_4_out, and_5_out, and_6_out, and_7_out;

  and and_1 (and_1_out, ~OP_1, ~OP_0);  // AND_Gate
  and and_2 (and_2_out, OP_1, ~OP_0, Funct[5], ~Funct[4], ~Funct[3], ~Funct[2], ~Funct[0]);  // AND_Gate
  and and_3 (and_3_out, OP_1, ~OP_0, Funct[5], ~Funct[4], Funct[3], ~Funct[2], Funct[1], ~Funct[0]);  // AND_Gate
  and and_4 (and_4_out, OP_1, ~OP_0, Funct[5], ~Funct[4], ~Funct[3], Funct[2], ~Funct[1], Funct[0]);  // AND_Gate
  and and_5 (and_5_out, OP_1, ~OP_0, Funct[5], ~Funct[4], Funct[3], ~Funct[2], Funct[1], ~Funct[0]);  // AND_Gate
  and and_6 (and_6_out, ~OP_1, OP_0);  // AND_Gate
  and and_7 (and_7_out, OP_1, ~OP_0, Funct[5], ~Funct[4], ~Funct[2], Funct[1], ~Funct[0]);  // AND_Gate
  or or_1 (OP[3], and_4_out, and_5_out);
  or or_2 (OP[1], and_6_out, and_7_out);
  or or_3 (OP[2], and_6_out, and_1_out, and_2_out, and_3_out);

  assign OP[0] = 1'b0;
endmodule

module shift_left (
  input  [31:0] Shift_in,
  output [31:0] Shift_out
);


  assign Shift_out = {Shift_in[29:0], 2'b00};
endmodule

module shift2628 (
  input  [25:0] in_1,
  output [27:0] out_2
);


  assign out_2 = {in_1, 2'b00};
endmodule
